# Fritzing sketch Vibration and RFID (saved by Fritzing 0.9.9b)
breadboards: 1

parts:
  Argon1 = Particle Argon
  Piezoelectric_Sensor1 = Piezoelectric Sensor
  U1 = V_REG_LD1085 [package=d2pack_a]
  Part1 = Adafruit MicroSD card breakout board [part_number="Adafruit #254"]
  S1 = Pushbutton [package="[THT]"]
  R1 = Resistor [tolerance=±5% resistance=100 package="0402 [SMD]"]
  U2 = ENCODER_RGB [package=encoder_led_2]
  OLED_I2C1 = OLED 128x64 I2C Monochrome Display
  RFID1 = RFID Reader

nets:
  3.3V: Argon1.3.3V, Part1.+3V3, S1.Pin_3, S1.Pin_4, OLED_I2C1.VDD, RFID1.ANT1
  GND: Argon1.GND, Part1.GND, R1.Pin_1, U2.G, OLED_I2C1.GND, RFID1.CP
  N1: Argon1.A5, Part1.CS
  N2: Argon1.SCK, Part1.CLK
  N3: Argon1.MO, Part1.DI
  N4: Argon1.MI, Part1.DO
  N5: Argon1.SDA, OLED_I2C1.SDA, RFID1.GND, RFID1.RES
  N6: Argon1.SCL, OLED_I2C1.SCK, RFID1.ANT0
  N7: Argon1.D5, S1.Pin_1, S1.Pin_2, R1.Pin_0
  N8: Piezoelectric_Sensor1.GND, U1.OUT
  N9: Piezoelectric_Sensor1.VCC, U1.IN

custom parts:
  Particle Argon: The Argon is a powerful Wi-Fi enabled development board that can act as either a standalone Wi-Fi endpoint or Wi-Fi enabled gateway for Particle Mesh networks. It is based on the Nordic nRF52840 and has built-in battery charging circuitry so it’s easy to connect a Li-Po and deploy your local network in minutes. The Argon is great for connecting existing projects to the Particle Device Cloud or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
  Piezoelectric Sensor: Piezoelectric sensor.
  Adafruit MicroSD card breakout board: Not just a simple breakout board, this microSD adapter goes the extra mile - designed for ease of use. Onboard 5v->3v regulator provides 150mA for power-hungry cards 3v level shifting means you can use this with ease on either 3v or 5v systems Uses a proper level shifting chip, not resistors: less problems, and faster read/write access Use 3 or 4 digital pins to read and write 2Gb+ of storage!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
  Pushbutton: A generic pushbutton.
  ENCODER_RGB: SparkFun RGB rotary Encoder
